// Digital circuit MUX.dig as structural Verilog
module MUX (
  input  D,
  input  C,
  input  B,
  input  A,
  output Y
);

  wire not_1_out, not_2_out, not_3_out, not_4_out;

  not not_1 (not_1_out, A);
  not not_2 (not_2_out, A);
  not not_3 (not_3_out, A);
  not not_4 (not_4_out, A);
  Multiplexer #(.Selector_Bits(3)) multiplexer_1 (
    .sel({B, C, D}), .in_0(A), .in_1(not_1_out), .in_2(A), .in_3(not_2_out), .in_4(A), .in_5(not_3_out),
    .in_6(A), .in_7(not_4_out), .out(Y));

  // Notes on the sheet:
  //   Use A as the most-significant bit and 
  //   D as the least-significant bit.
  //   Converts between single bits & a 3-bit bus
endmodule

/* Test case:
A B C D Y
0 0 0 0 X
0 0 0 1 1
0 0 1 0 0
0 0 1 1 1
0 1 0 0 0
0 1 0 1 1
0 1 1 0 0
0 1 1 1 1
1 0 0 0 1
1 0 0 1 0
1 0 1 0 1
1 0 1 1 0
1 1 0 0 1
1 1 0 1 X
1 1 1 0 X
1 1 1 1 X
*/
